# Fritzing sketch breadboard_layout (saved by Fritzing 0.9.3b)
circuit board: 8.46667cm x 5.64444cm
breadboards: 1

parts:
  Part1 = Arduino Uno (Rev3) - ICSP
  IR1 = TSOP312.., 314.. [package=THT]
  LED1 = LEDs [package=led10mm]
  LED2 = LEDs [package=led10mm]
  R1 = Resistor [tolerance=±5% resistance=680 package="2010 [SMD]"]
  R2 = Resistor [tolerance=±5% resistance=470 package="2010 [SMD]"]

nets:
  N1: Part1.5V, IR1.Vs
  GND: Part1.GND, IR1.GND, LED1.C, LED2.C
  N2: Part1.D8, R2.Pin_1
  N3: Part1.D4, IR1.Data
  N4: Part1.D7, R1.Pin_0
  N5: LED1.A, R2.Pin_0
  N6: LED2.A, R1.Pin_1
