# Fritzing sketch circuit (saved by Fritzing 0.9.3b)
circuit board: 5.47596cm x 5.81293cm
breadboards: 1

parts:
  CPU = Arduino Uno (Rev3) - ICSP  # not connected
  HC-SR04_Sensor_1 = HC-SR04 Ultrasonic Distance Sensor  # not connected
  Q1 = TRANSISTOR_NPN [package=to-92]
  R1 = Resistor [tolerance=±5% resistance=68k package="0603 [SMD]"]
  RELAY = female pin header, 3 pins [form="♀ (female)"]
  LO-LIM = POT [package=trim_pot]
  R2 = Resistor [tolerance=±5% resistance=10k package="0603 [SMD]"]
  HI-LIM = POT [package=trim_pot]
  R3 = Resistor [tolerance=±5% resistance=10k package="0603 [SMD]"]
  SENSOR = female pin header, 4 pins [form="♀ (female)"]
  CTRL = female pin header, 8 pins [form="♀ (female)"]

nets:
  GND: Q1.E, RELAY.pin3, LO-LIM.A, HI-LIM.A, SENSOR.pin4, CTRL.pin3
  N1: Q1.B, R1.Pin_0
  N2: Q1.C, RELAY.pin1
  N3: R1.Pin_1, CTRL.pin5
  N4: RELAY.pin2, HI-LIM.E, SENSOR.pin1, CTRL.pin4
  N5: LO-LIM.S, R2.Pin_0
  N6: R2.Pin_1, CTRL.pin2
  N7: HI-LIM.S, R3.Pin_0
  N8: R3.Pin_1, CTRL.pin1
  N9: SENSOR.pin2, CTRL.pin6
  N10: SENSOR.pin3, CTRL.pin7

notes:
  A1
  A0
  GND
  5V
  10
  13
  12

// code stored in the sketch: main_circuit.ino
// what is this? A code editor???
void main() {
	System.out.println("Hello, world!");
}

// INTERESTING!!!

void setup() {
	// setup code
}

void loop() {
	// loop code
}
